// Logisim project 800x600_rr60_pf40d000.circ as structural Verilog: 1 circuit, main circuit main
module main (
);

  wire Access_RAM, and_1_out, and_2_out, and_3_out, and_4_out, and_5_out, and_6_out, and_7_out, and_8_out,
       H_BackPorch, H_FrontPorch, H_Sync, H_Visible, PixelClock, pull_resistor_3_node, pull_resistor_4_node,
       pull_resistor_6_node, pull_resistor_8_node, V_BackPorch, V_FrontPorch, V_Sync, V_Visible, VGA_13,
       VGA_14;
  wire [9:0] Counter_Vert_q;
  wire [10:0] Counter_Horz_q;

  Counter #(.max('h7ff), .width(11)) Counter_Horz (
    .clr(and_2_out), .load(1'b0), .up(1'b1), .count(1'b1), .clk(PixelClock), .Q(Counter_Horz_q));  // open: D, carry
  Counter #(.max('h3ff), .width(10)) Counter_Vert (
    .clr(and_4_out), .load(1'b0), .up(1'b1), .count(1'b1), .clk(and_2_out), .Q(Counter_Vert_q));  // open: D, carry
  and and_1 (and_1_out, ~Counter_Horz_q[10], Counter_Horz_q[9], Counter_Horz_q[8], ~Counter_Horz_q[7], ~Counter_Horz_q[6], Counter_Horz_q[5], ~Counter_Horz_q[4], ~Counter_Horz_q[3], ~Counter_Horz_q[2], ~Counter_Horz_q[1], ~Counter_Horz_q[0]);  // AND_Gate
  and and_2 (and_2_out, Counter_Horz_q[10], ~Counter_Horz_q[9], ~Counter_Horz_q[8], ~Counter_Horz_q[7], ~Counter_Horz_q[6], Counter_Horz_q[5], ~Counter_Horz_q[4], ~Counter_Horz_q[3], ~Counter_Horz_q[2], ~Counter_Horz_q[1], ~Counter_Horz_q[0]);  // AND_Gate
  and and_3 (and_3_out, Counter_Vert_q[9], ~Counter_Vert_q[8], ~Counter_Vert_q[7], Counter_Vert_q[6], ~Counter_Vert_q[5], Counter_Vert_q[4], Counter_Vert_q[3], ~Counter_Vert_q[2], ~Counter_Vert_q[1], ~Counter_Vert_q[0]);  // AND_Gate
  and and_4 (and_4_out, Counter_Vert_q[9], ~Counter_Vert_q[8], ~Counter_Vert_q[7], Counter_Vert_q[6], Counter_Vert_q[5], Counter_Vert_q[4], ~Counter_Vert_q[3], Counter_Vert_q[2], ~Counter_Vert_q[1], ~Counter_Vert_q[0]);  // AND_Gate
  and and_5 (and_5_out, ~Counter_Horz_q[10], Counter_Horz_q[9], Counter_Horz_q[8], ~Counter_Horz_q[7], Counter_Horz_q[6], ~Counter_Horz_q[5], ~Counter_Horz_q[4], Counter_Horz_q[3], ~Counter_Horz_q[2], ~Counter_Horz_q[1], ~Counter_Horz_q[0]);  // AND_Gate
  and and_6 (and_6_out, ~Counter_Horz_q[10], Counter_Horz_q[9], Counter_Horz_q[8], Counter_Horz_q[7], Counter_Horz_q[6], ~Counter_Horz_q[5], ~Counter_Horz_q[4], Counter_Horz_q[3], ~Counter_Horz_q[2], ~Counter_Horz_q[1], ~Counter_Horz_q[0]);  // AND_Gate
  and and_7 (and_7_out, Counter_Vert_q[9], ~Counter_Vert_q[8], ~Counter_Vert_q[7], Counter_Vert_q[6], ~Counter_Vert_q[5], Counter_Vert_q[4], Counter_Vert_q[3], ~Counter_Vert_q[2], ~Counter_Vert_q[1], Counter_Vert_q[0]);  // AND_Gate
  and and_8 (and_8_out, Counter_Vert_q[9], ~Counter_Vert_q[8], ~Counter_Vert_q[7], Counter_Vert_q[6], ~Counter_Vert_q[5], Counter_Vert_q[4], Counter_Vert_q[3], Counter_Vert_q[2], ~Counter_Vert_q[1], Counter_Vert_q[0]);  // AND_Gate
  Pull_Resistor pull_resistor_1 (.node(Counter_Horz_q));
  Pull_Resistor pull_resistor_2 (.node(Counter_Vert_q));
  S_R_Flip_Flop #(.trigger("high")) s_r_ff_1 (
    .S(and_2_out), .R(and_1_out), .clk(pull_resistor_3_node), .Q(H_Visible));  // open: reset, Qn, preset
  S_R_Flip_Flop #(.trigger("high")) s_r_ff_2 (
    .S(and_1_out), .R(and_5_out), .clk(pull_resistor_3_node), .Q(H_FrontPorch));  // open: reset, Qn, preset
  S_R_Flip_Flop #(.trigger("high")) s_r_ff_3 (
    .S(and_5_out), .R(and_6_out), .clk(pull_resistor_3_node), .Q(H_Sync));  // open: reset, Qn, preset
  S_R_Flip_Flop #(.trigger("high")) s_r_ff_4 (
    .S(and_6_out), .R(and_2_out), .clk(pull_resistor_3_node), .Q(H_BackPorch));  // open: reset, Qn, preset
  Pull_Resistor #(.pull(1)) pull_resistor_3 (.node(pull_resistor_3_node));
  S_R_Flip_Flop #(.trigger("high")) s_r_ff_5 (
    .S(and_4_out), .R(and_3_out), .clk(pull_resistor_4_node), .Q(V_Visible));  // open: reset, Qn, preset
  S_R_Flip_Flop #(.trigger("high")) s_r_ff_6 (
    .S(and_3_out), .R(and_7_out), .clk(pull_resistor_4_node), .Q(V_FrontPorch));  // open: reset, Qn, preset
  S_R_Flip_Flop #(.trigger("high")) s_r_ff_7 (
    .S(and_7_out), .R(and_8_out), .clk(pull_resistor_4_node), .Q(V_Sync));  // open: reset, Qn, preset
  S_R_Flip_Flop #(.trigger("high")) s_r_ff_8 (
    .S(and_8_out), .R(and_4_out), .clk(pull_resistor_4_node), .Q(V_BackPorch));  // open: reset, Qn, preset
  Pull_Resistor #(.pull(1)) pull_resistor_4 (.node(pull_resistor_4_node));
  Clock Clk_40d000MHz (.out(PixelClock));
  and and_9 (Access_RAM, H_Visible, V_Visible);
  Pull_Resistor #(.pull(1)) pull_resistor_5 (.node(VGA_13));
  Transistor #(.\type ("n")) transistor_1 (.in(1'b0), .out(VGA_13), .gate(pull_resistor_6_node));
  Pull_Resistor #(.pull(1)) pull_resistor_6 (.node(pull_resistor_6_node));
  Transistor #(.\type ("n")) transistor_2 (.in(1'b0), .out(pull_resistor_6_node), .gate(H_Sync));
  Pull_Resistor #(.pull(1)) pull_resistor_7 (.node(VGA_14));
  Transistor #(.\type ("n")) transistor_3 (.in(1'b0), .out(VGA_14), .gate(pull_resistor_8_node));
  Pull_Resistor #(.pull(1)) pull_resistor_8 (.node(pull_resistor_8_node));
  Transistor #(.\type ("n")) transistor_4 (.in(1'b0), .out(pull_resistor_8_node), .gate(V_Sync));

  // Notes on the sheet:
  //   Circuit version: 1.0 (01/11/2025 23:07 GMT+7)
  //   Features in progress: IRQ circuitry to access RAM when need to display video pixels
endmodule
